# Fritzing sketch PCB (saved by Fritzing 0.9.3b)
circuit board: 3.52718cm x 2.33296cm
breadboards: 1

parts:
  IC1 = ADS1115 16-bit ADC Breakout
  Part1 = Soil Moisture Sensor
  Raspberry_Pi1 = Raspberry Pi B rev2
  C1 = Electrolytic Capacitor [capacitance=1µF voltage=6.3V package="100 mil [THT, electrolytic]"]
  R1 = Photocell (LDR) [package=THT]
  S4 = Magnetic Door Switch [package=reed_switch_plastic]

nets:
  VDD: IC1.VDD, Part1.VCC, Raspberry_Pi1.3V3, R1.pin_1
  GND: IC1.GND, Part1.GND, Raspberry_Pi1.GND, C1.-, S4.2
  N1: IC1.SCL, Raspberry_Pi1.GPIO_3
  N2: IC1.SDA, Raspberry_Pi1.GPIO_2
  N3: IC1.A0, Part1.SIG
  N4: Raspberry_Pi1.GPIO_4, S4.1
  N5: C1.+, R1.pin_0

custom parts:
  ADS1115 16-bit ADC Breakout: ADS1015 12-bit I2C ADC+PGA Breakout
