# Fritzing sketch RaspiGuard Schematic 2.0 (saved by Fritzing 0.9.3b)
breadboards: 1

parts:
  Raspberry_Pi3 = Raspberry Pi B rev2
  Part1 = Adafruit ADS1115 16Bit I2C ADC [part_number="Adafruit #1085"]
  R5 = PHOTOCELL [package=photocell]
  R6 = Resistor [tolerance=±5% resistance=10 package=THT]
  S6 = Magnetic Door Switch [package=reed_switch_plastic]
  Part2 = Soil Moisture Sensor

nets:
  3V3: Raspberry_Pi3.3V3, Part1.VDD, Part2.VCC
  N1: Raspberry_Pi3.GPIO_2, Part1.SDA
  N2: Raspberry_Pi3.GPIO_3, Part1.SCL
  GND: Raspberry_Pi3.GND, Part1.GND, R6.Pin_1, S6.2, Part2.GND
  N3: Raspberry_Pi3.GPIO_4, S6.1
  N4: Part1.AIN1, Part2.SIG
  N5: Part1.AIN0, R5.P$2, R6.Pin_0

custom parts:
  Adafruit ADS1115 16Bit I2C ADC: For microcontrollers without an analog-to-digital converter or when you want a higher-precision ADC, the ADS1115 provides 16-bit precision at 860 samples/second over I2C. The chip can be configured as 4 single-ended input channels, or two differential channels. As a nice bonus, it even includes a programmable gain amplifier, up to x16, to help boost up smaller single/differential signals to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
